// Logisim project FULLADDER14NOVEMBER.circ as structural Verilog: 23 circuits, main circuit FourBitTwosComplement
module FourBitTwosComplement (
  input  [3:0] A,
  input  in_2,
  input  [3:0] B,
  input  in_4,
  input  subtractcontrol,
  output [3:0] sum,
  output cout
);

  wire fulladder_1_carry_out, fulladder_2_carry_out, fulladder_3_carry_out, xor_1_out, xor_2_out, xor_3_out,
       xor_4_out;
  wire [3:0] fulladder_1_sum_out, register_1_q, register_2_q;

  Register #(.width(4)) register_1 (.D(A), .clk(in_2), .Q(register_1_q));  // open: en, clr
  Register #(.width(4)) register_2 (.D(B), .clk(in_2), .Q(register_2_q));  // open: en, clr
  // Probe on register_1_q
  // Probe on register_2_q
  xor xor_1 (xor_1_out, subtractcontrol, register_2_q[0]);
  xor xor_2 (xor_2_out, subtractcontrol, register_2_q[1]);
  xor xor_3 (xor_3_out, subtractcontrol, register_2_q[2]);
  xor xor_4 (xor_4_out, subtractcontrol, register_2_q[3]);
  FullAdder fulladder_1 (
    .A(register_1_q[0]), .B(xor_1_out), .carry_in(subtractcontrol), .sum_out(fulladder_1_sum_out[0]),
    .carry_out(fulladder_1_carry_out));
  FullAdder fulladder_2 (
    .A(register_1_q[1]), .B(xor_2_out), .carry_in(fulladder_1_carry_out), .sum_out(fulladder_1_sum_out[1]),
    .carry_out(fulladder_2_carry_out));
  FullAdder fulladder_3 (
    .A(register_1_q[2]), .B(xor_3_out), .carry_in(fulladder_2_carry_out), .sum_out(fulladder_1_sum_out[2]),
    .carry_out(fulladder_3_carry_out));
  FullAdder fulladder_4 (
    .A(register_1_q[3]), .B(xor_4_out), .carry_in(fulladder_3_carry_out), .sum_out(fulladder_1_sum_out[3]),
    .carry_out(cout));
  Register #(.width(4)) register_3 (.D(fulladder_1_sum_out), .clk(in_4), .Q(sum));  // open: en, clr
endmodule

module FullAdder (
  input  A,
  input  B,
  input  carry_in,
  output sum_out,
  output carry_out
);

  wire and_1_out, final_carry_out, sum_intermediate_out;

  xor sum_intermediate (sum_intermediate_out, A, B);
  and final_carry (final_carry_out, sum_intermediate_out, carry_in);
  and and_1 (and_1_out, B, A);
  xor final_sum (sum_out, sum_intermediate_out, carry_in);
  or or_1 (carry_out, final_carry_out, and_1_out);
endmodule

module FourBitAdder (
  input  in_1
);

  wire fulladder_1_carry_out, fulladder_2_carry_out, fulladder_3_carry_out, fulladder_4_carry_out;
  wire [3:0] A_q, B_q, fulladder_1_sum_out, register_1_q;

  Register #(.width(4)) A (.Q(A_q));  // open: D, en, clk, clr
  Register #(.width(4)) B (.Q(B_q));  // open: D, en, clk, clr
  // Probe on A_q
  // Probe on B_q
  FullAdder fulladder_1 (
    .A(A_q[0]), .B(B_q[0]), .sum_out(fulladder_1_sum_out[0]), .carry_out(fulladder_1_carry_out));  // open: carry_in
  FullAdder fulladder_2 (
    .A(A_q[1]), .B(B_q[1]), .carry_in(fulladder_1_carry_out), .sum_out(fulladder_1_sum_out[1]),
    .carry_out(fulladder_2_carry_out));
  FullAdder fulladder_3 (
    .A(A_q[2]), .B(B_q[2]), .carry_in(fulladder_2_carry_out), .sum_out(fulladder_1_sum_out[2]),
    .carry_out(fulladder_3_carry_out));
  FullAdder fulladder_4 (
    .A(A_q[3]), .B(B_q[3]), .carry_in(fulladder_3_carry_out), .sum_out(fulladder_1_sum_out[3]),
    .carry_out(fulladder_4_carry_out));
  Register #(.width(4)) register_1 (.D(fulladder_1_sum_out), .clk(in_1), .Q(register_1_q));  // open: en, clr
  LED led_1 (.in(fulladder_4_carry_out));
  // Probe on register_1_q
endmodule

module memorycell_flipflops (
  input  Clock,
  input  WE,
  input  Din,
  input  OE,
  input  Reset,
  output Dout,
  output StoredData
);

  wire and_1_out, and_2_out, not_1_out, or_1_out;

  not not_1 (not_1_out, WE);
  and and_1 (and_1_out, StoredData, not_1_out);
  and and_2 (and_2_out, WE, Din);
  or or_1 (or_1_out, and_1_out, and_2_out);
  D_Flip_Flop TwoNOR (.clk(Clock), .D(or_1_out), .Q(StoredData), .reset(Reset));  // open: Qn, preset
  assign Dout = OE ? StoredData : 1'bz;  // Controlled_Buffer controlled_buffer_1

  // Notes on the sheet:
  //   001
  //   110
endmodule

module EightBitRegister (
  input  Clock,
  input  WE,
  input  OE,
  input  [7:0] Din,
  output [7:0] Dout,
  output [7:0] StoredData
);

  memorycell_flipflops Zero (
    .Clock(Clock), .WE(WE), .Din(Din[0]), .OE(OE), .Dout(Dout[0]), .StoredData(StoredData[0]));  // open: Reset
  memorycell_flipflops One (
    .Clock(Clock), .WE(WE), .Din(Din[1]), .OE(OE), .Dout(Dout[1]), .StoredData(StoredData[1]));  // open: Reset
  memorycell_flipflops Two (
    .Clock(Clock), .WE(WE), .Din(Din[2]), .OE(OE), .Dout(Dout[2]), .StoredData(StoredData[2]));  // open: Reset
  memorycell_flipflops Three (
    .Clock(Clock), .WE(WE), .Din(Din[3]), .OE(OE), .Dout(Dout[3]), .StoredData(StoredData[3]));  // open: Reset
  memorycell_flipflops Four (
    .Clock(Clock), .WE(WE), .Din(Din[4]), .OE(OE), .Dout(Dout[4]), .StoredData(StoredData[4]));  // open: Reset
  memorycell_flipflops Five (
    .Clock(Clock), .WE(WE), .Din(Din[5]), .OE(OE), .Dout(Dout[5]), .StoredData(StoredData[5]));  // open: Reset
  memorycell_flipflops Six (
    .Clock(Clock), .WE(WE), .Din(Din[6]), .OE(OE), .Dout(Dout[6]), .StoredData(StoredData[6]));  // open: Reset
  memorycell_flipflops Seven (
    .Clock(Clock), .WE(WE), .Din(Din[7]), .OE(OE), .Dout(Dout[7]), .StoredData(StoredData[7]));  // open: Reset
endmodule

module MAR (
  input  Clock,
  input  WE,
  input  OE,
  input  [3:0] Din,
  output [3:0] Dout,
  output [3:0] StoredData
);

  memorycell_flipflops Zero (
    .Clock(Clock), .WE(WE), .Din(Din[0]), .OE(OE), .Dout(Dout[0]), .StoredData(StoredData[0]));  // open: Reset
  memorycell_flipflops One (
    .Clock(Clock), .WE(WE), .Din(Din[1]), .OE(OE), .Dout(Dout[1]), .StoredData(StoredData[1]));  // open: Reset
  memorycell_flipflops Two (
    .Clock(Clock), .WE(WE), .Din(Din[2]), .OE(OE), .Dout(Dout[2]), .StoredData(StoredData[2]));  // open: Reset
  memorycell_flipflops Three (
    .Clock(Clock), .WE(WE), .Din(Din[3]), .OE(OE), .Dout(Dout[3]), .StoredData(StoredData[3]));  // open: Reset
endmodule

module OneBitALU (
  input  Subtract,
  input  Cin,
  input  [2:0] op,
  input  A,
  input  B,
  input  Less,
  output Result,
  output out_8,
  output Set
);

  wire and_1_out, nor_1_out, or_1_out, xor_1_out, xor_2_out;

  xor xor_1 (xor_1_out, B, Subtract);
  and and_1 (and_1_out, A, B);
  or or_1 (or_1_out, A, B);
  xor xor_2 (xor_2_out, A, B);
  nor nor_1 (nor_1_out, A, B);
  Adder #(.width(1)) adder_1 (.a(A), .b(xor_1_out), .out(Set), .cin(Cin), .cout(out_8));
  Multiplexer #(.disabled("Z"), .select(3)) multiplexer_1 (
    .in0(and_1_out), .in1(or_1_out), .in2(xor_2_out), .in3(nor_1_out), .in4(Set), .in5(Less), .out(Result),
    .sel(op));  // open: in6, in7
endmodule

module EightBitTwosComplement (
  input  [7:0] A,
  input  [7:0] B,
  input  subtractcontrol,
  output [7:0] out_4,
  output cout
);

  wire fulladder_1_carry_out, fulladder_2_carry_out, fulladder_3_carry_out, fulladder_4_carry_out,
       fulladder_5_carry_out, fulladder_6_carry_out, fulladder_7_carry_out, xor_1_out, xor_2_out, xor_3_out,
       xor_4_out, xor_5_out, xor_6_out, xor_7_out, xor_8_out;

  xor xor_1 (xor_1_out, subtractcontrol, B[0]);
  xor xor_2 (xor_2_out, subtractcontrol, B[1]);
  xor xor_3 (xor_3_out, subtractcontrol, B[2]);
  xor xor_4 (xor_4_out, subtractcontrol, B[3]);
  xor xor_5 (xor_5_out, subtractcontrol, B[4]);
  xor xor_6 (xor_6_out, subtractcontrol, B[5]);
  xor xor_7 (xor_7_out, subtractcontrol, B[6]);
  xor xor_8 (xor_8_out, subtractcontrol, B[7]);
  FullAdder fulladder_1 (
    .A(A[0]), .B(xor_1_out), .carry_in(subtractcontrol), .sum_out(out_4[0]), .carry_out(fulladder_1_carry_out));
  FullAdder fulladder_2 (
    .A(A[1]), .B(xor_2_out), .carry_in(fulladder_1_carry_out), .sum_out(out_4[1]),
    .carry_out(fulladder_2_carry_out));
  FullAdder fulladder_3 (
    .A(A[2]), .B(xor_3_out), .carry_in(fulladder_2_carry_out), .sum_out(out_4[2]),
    .carry_out(fulladder_3_carry_out));
  FullAdder fulladder_4 (
    .A(A[3]), .B(xor_4_out), .carry_in(fulladder_3_carry_out), .sum_out(out_4[3]),
    .carry_out(fulladder_4_carry_out));
  FullAdder fulladder_5 (
    .A(A[4]), .B(xor_5_out), .carry_in(fulladder_4_carry_out), .sum_out(out_4[4]),
    .carry_out(fulladder_5_carry_out));
  FullAdder fulladder_6 (
    .A(A[5]), .B(xor_6_out), .carry_in(fulladder_5_carry_out), .sum_out(out_4[5]),
    .carry_out(fulladder_6_carry_out));
  FullAdder fulladder_7 (
    .A(A[6]), .B(xor_7_out), .carry_in(fulladder_6_carry_out), .sum_out(out_4[6]),
    .carry_out(fulladder_7_carry_out));
  FullAdder fulladder_8 (
    .A(A[7]), .B(xor_8_out), .carry_in(fulladder_7_carry_out), .sum_out(out_4[7]), .carry_out(cout));
endmodule

module DawitsALU (
  input  in_1,
  input  [2:0] op_select,
  input  in_3,
  input  [3:0] A,
  input  [3:0] B,
  output [3:0] result,
  output out_7
);

  wire onebitalu_1_out_8, onebitalu_2_out_8, onebitalu_3_out_8, onebitalu_4_set;

  OneBitALU onebitalu_1 (
    .Subtract(in_1), .Cin(in_1), .op(op_select), .A(A[0]), .B(B[0]), .Less(onebitalu_4_set),
    .Result(result[0]), .out_8(onebitalu_1_out_8));  // open: Set
  OneBitALU onebitalu_2 (
    .Subtract(in_1), .Cin(onebitalu_1_out_8), .op(op_select), .A(A[1]), .B(B[1]), .Less(in_3),
    .Result(result[1]), .out_8(onebitalu_2_out_8));  // open: Set
  OneBitALU onebitalu_3 (
    .Subtract(in_1), .Cin(onebitalu_2_out_8), .op(op_select), .A(A[2]), .B(B[2]), .Less(in_3),
    .Result(result[2]), .out_8(onebitalu_3_out_8));  // open: Set
  OneBitALU onebitalu_4 (
    .Subtract(in_1), .Cin(onebitalu_3_out_8), .op(op_select), .A(A[3]), .B(B[3]), .Less(in_3),
    .Result(result[3]), .Set(onebitalu_4_set));  // open: out_8
  nor nor_1 (out_7, result[0], result[1], result[2], result[2]);
endmodule

module MUX4by1 (
  input  [7:0] E11,
  input  [7:0] E10,
  input  [7:0] E01,
  input  [7:0] E00,
  input  S1,
  input  S0,
  output [7:0] out_7
);

  wire [7:0] and_1_out, and_2_out, and_3_out, and_4_out, bit_extender_1_out, bit_extender_2_out, not_1_out,
       not_2_out;

  assign bit_extender_1_out = {{7{S1}}, S1};  // Bit_Extender bit_extender_1
  assign bit_extender_2_out = {{7{S0}}, S0};  // Bit_Extender bit_extender_2
  assign not_1_out = ~bit_extender_1_out;  // NOT_Gate not_1, 8 bits wide
  assign not_2_out = ~bit_extender_2_out;  // NOT_Gate not_2, 8 bits wide
  assign and_1_out = E11 & bit_extender_1_out & bit_extender_2_out;  // AND_Gate and_1, 8 bits wide
  assign and_2_out = E10 & not_1_out & bit_extender_2_out;  // AND_Gate and_2, 8 bits wide
  assign and_3_out = E01 & bit_extender_1_out;  // AND_Gate and_3, 8 bits wide
  assign and_4_out = E00 & not_1_out & not_2_out;  // AND_Gate and_4, 8 bits wide
  assign out_7 = and_1_out | and_2_out | and_3_out | and_4_out;  // OR_Gate or_1, 8 bits wide
endmodule

module Shift_4 (
  input  b3,
  input  b2,
  input  b1,
  input  b0,
  input  Right,
  input  Left,
  output R2,
  output L3,
  output R1,
  output L2,
  output R0,
  output L1
);

  and and_1 (R2, b3, Right);
  and and_2 (L3, Left, b2);
  and and_3 (R1, b2, Right);
  and and_4 (L2, Left, b1);
  and and_5 (R0, b1, Right);
  and and_6 (L1, Left, b0);
endmodule

module EightBitAND (
  input  [7:0] A,
  input  [7:0] B,
  output [7:0] ANDOUT
);

  and and_1 (ANDOUT[7], A[7], B[7]);
  and and_2 (ANDOUT[6], A[6], B[6]);
  and and_3 (ANDOUT[5], A[5], B[5]);
  and and_4 (ANDOUT[4], A[4], B[4]);
  and and_5 (ANDOUT[3], A[3], B[3]);
  and and_6 (ANDOUT[2], A[2], B[2]);
  and and_7 (ANDOUT[1], A[1], B[1]);
  and and_8 (ANDOUT[0], A[0], B[0]);
endmodule

module EightBitOR (
  input  [7:0] A,
  input  [7:0] B,
  output [7:0] OROUT
);

  or or_1 (OROUT[7], A[7], B[7]);
  or or_2 (OROUT[6], A[6], B[6]);
  or or_3 (OROUT[5], A[5], B[5]);
  or or_4 (OROUT[4], A[4], B[4]);
  or or_5 (OROUT[3], A[3], B[3]);
  or or_6 (OROUT[2], A[2], B[2]);
  or or_7 (OROUT[1], A[1], B[1]);
  or or_8 (OROUT[0], A[0], B[0]);
endmodule

module EightBitXOR (
  input  [7:0] A,
  input  [7:0] B,
  output [7:0] XOROUT
);

  xor xor_1 (XOROUT[7], A[7], B[7]);
  xor xor_2 (XOROUT[6], A[6], B[6]);
  xor xor_3 (XOROUT[5], A[5], B[5]);
  xor xor_4 (XOROUT[4], A[4], B[4]);
  xor xor_5 (XOROUT[3], A[3], B[3]);
  xor xor_6 (XOROUT[2], A[2], B[2]);
  xor xor_7 (XOROUT[1], A[1], B[1]);
  xor xor_8 (XOROUT[0], A[0], B[0]);
endmodule

module ALU_REDESIGN (
  input  [7:0] A,
  input  [7:0] B,
  input  OE,
  input  subtractcontrol,
  input  direction,
  input  S1,
  input  S0,
  output [7:0] result,
  output [7:0] Dout,
  output cout
);

  wire [7:0] eightbitand_1_andout, eightbitor_1_orout, eightbittwoscomplement_1_out_4, shifter_8_1_o;

  EightBitTwosComplement eightbittwoscomplement_1 (
    .A(A), .B(B), .subtractcontrol(subtractcontrol), .out_4(eightbittwoscomplement_1_out_4), .cout(cout));
  SHIFTER_8 shifter_8_1 (.I(A), .Direction(direction), .O(shifter_8_1_o));
  EightBitAND eightbitand_1 (.A(A), .B(B), .ANDOUT(eightbitand_1_andout));
  EightBitOR eightbitor_1 (.A(A), .B(B), .OROUT(eightbitor_1_orout));
  MUX4by1 mux4by1_1 (
    .E11(eightbitor_1_orout), .E10(eightbitand_1_andout), .E01(shifter_8_1_o),
    .E00(eightbittwoscomplement_1_out_4), .S1(S1), .S0(S0), .out_7(result));
  assign Dout = OE ? result : 8'bz;  // Controlled_Buffer controlled_buffer_1

  // Notes on the sheet:
  //   00
  //   01
  //   10
  //   11
endmodule

module SHIFTER_8 (
  input  [7:0] I,
  input  Direction,
  output [7:0] O
);

  wire and_1_out, and_3_out, and_4_out, and_5_out, and_6_out, and_7_out, and_8_out, and_9_out, and_10_out,
       and_11_out, and_12_out, and_14_out, not_1_out;

  // Probe on I
  not not_1 (not_1_out, Direction);
  and and_1 (and_1_out, I[0], not_1_out);
  and and_2 (O[0], Direction, I[1]);
  or or_1 (O[1], and_1_out, and_4_out);
  and and_3 (and_3_out, I[1], I[2]);
  and and_4 (and_4_out, Direction, I[2]);
  and and_5 (and_5_out, I[2], not_1_out);
  or or_2 (O[2], and_3_out, and_6_out);
  and and_6 (and_6_out, Direction, I[3]);
  or or_3 (O[3], and_5_out, and_8_out);
  and and_7 (and_7_out, I[3], not_1_out);
  and and_8 (and_8_out, Direction, I[4]);
  and and_9 (and_9_out, I[4], not_1_out);
  or or_4 (O[4], and_7_out, and_10_out);
  and and_10 (and_10_out, Direction, I[5]);
  or or_5 (O[5], and_9_out, and_12_out);
  and and_11 (and_11_out, I[5], not_1_out);
  and and_12 (and_12_out, Direction, I[6]);
  and and_13 (O[7], I[6], not_1_out);
  or or_6 (O[6], and_11_out, and_14_out);
  // Probe on O
  and and_14 (and_14_out, Direction, I[7]);

  // Notes on the sheet:
  //   0 - Right (Divide)
  //   1 - Left (Multiply)
endmodule

module MUX8to1 (
  input  S2,
  input  S1,
  input  S0,
  input  E000,
  input  E001,
  input  E010,
  input  E011,
  input  E100,
  input  E101,
  input  E110,
  input  E111,
  output out_12
);

  wire not_1_out, not_3_out, oneoneone_out, oneonezero_out, onezerone_out, onezerozero_out, zerooneone_out,
       zeroonezero_out, zerozeroone_out, zerozerozero_out;

  not not_1 (not_1_out, S1);
  not not_2 (not_1_out, S1);
  not not_3 (not_3_out, S0);
  and zerozerozero (zerozerozero_out, E000, not_3_out, not_1_out, not_1_out);
  and zerozeroone (zerozeroone_out, E001, S0, not_1_out, not_1_out);
  and zeroonezero (zeroonezero_out, E010, not_3_out, S1, not_1_out);
  and zerooneone (zerooneone_out, E011, not_3_out, S1, S1);
  and onezerozero (onezerozero_out, E100, S0, not_3_out, not_1_out);
  and onezerone (onezerone_out, E101, S0, not_1_out, S1);
  and oneonezero (oneonezero_out, E110, not_3_out, S1, S1);
  and oneoneone (oneoneone_out, E111, S0, S1, S1);
  or or_1 (out_12, zerozerozero_out, zerozeroone_out, zeroonezero_out, zerooneone_out, onezerozero_out, onezerone_out, oneonezero_out, oneoneone_out);

  assign S2 = S1;

  // Notes on the sheet:
  //   000, 001, 010, 011, 100, 101, 110, 111
endmodule

module CPU (
  input  in_1,
  input  [3:0] in_2,
  input  [7:0] in_3,
  input  TestingOE,
  output [3:0] CounterContent,
  output [3:0] MAR_Content,
  output [7:0] IR_content,
  output [7:0] MBR_Content,
  output [7:0] RegisterA_content,
  output [7:0] ALU_result,
  output [7:0] out_11,
  output [2:0] StepContent,
  output [7:0] RegisterB_content
);

  wire clock_1_out, cu_full1_1_c0, cu_full1_1_c1, cu_full1_1_c2, cu_full1_1_c3, cu_full1_1_c4, cu_full1_1_c5,
       cu_full1_1_c6, cu_full1_1_c7, cu_full1_1_c8, cu_full1_1_c9, cu_full1_1_c10, cu_full1_1_c11,
       cu_full1_1_c12, cu_full1_1_c13, cu_full1_1_c14, cu_full1_1_c15, cu_full1_1_c16, cu_full1_1_c17,
       cu_full1_1_c18, cu_full1_1_c19;
  wire [3:0] bitselector_2_out, controlled_buffer_1_out, mar_1_dout;
  wire [7:0] alu_redesign_1_dout, InstructionRegister_dout, ram_1_dout;

  Clock clock_1 (.out(clock_1_out));
  Counter #(.max('h3), .width(4)) ProgramCounter (
    .D(controlled_buffer_1_out), .count(cu_full1_1_c1), .Q(CounterContent), .clk(clock_1_out));  // open: load, carry, up, clr
  assign controlled_buffer_1_out = cu_full1_1_c0 ? CounterContent : 4'bz;  // Controlled_Buffer controlled_buffer_1
  EightBitRegister InstructionRegister (
    .Clock(clock_1_out), .WE(cu_full1_1_c7), .OE(cu_full1_1_c8), .Din(alu_redesign_1_dout),
    .Dout(InstructionRegister_dout), .StoredData(IR_content));
  EightBitRegister RegisterA (
    .Clock(clock_1_out), .WE(cu_full1_1_c12), .Din(alu_redesign_1_dout), .StoredData(RegisterA_content));  // open: OE, Dout
  ALU_REDESIGN alu_redesign_1 (
    .A(RegisterA_content), .B(RegisterB_content), .OE(cu_full1_1_c11), .subtractcontrol(cu_full1_1_c18),
    .direction(cu_full1_1_c19), .S1(cu_full1_1_c17), .S0(cu_full1_1_c16), .result(ALU_result),
    .Dout(alu_redesign_1_dout));  // open: cout
  EightBitRegister RegisterB (
    .Clock(clock_1_out), .WE(cu_full1_1_c13), .Din(alu_redesign_1_dout), .StoredData(RegisterB_content));  // open: OE, Dout
  BitSelector #(.group(4)) bitselector_1 (.in(InstructionRegister_dout), .out(controlled_buffer_1_out), .sel(1'b0));
  LED D7 (.in(alu_redesign_1_dout[7]));
  LED D6 (.in(alu_redesign_1_dout[6]));
  LED D5 (.in(alu_redesign_1_dout[5]));
  LED D4 (.in(alu_redesign_1_dout[4]));
  assign alu_redesign_1_dout = TestingOE ? in_3 : 8'bz;  // Controlled_Buffer controlled_buffer_2
  LED D3 (.in(alu_redesign_1_dout[3]));
  LED D2 (.in(alu_redesign_1_dout[2]));
  LED D1 (.in(alu_redesign_1_dout[1]));
  LED D0 (.in(alu_redesign_1_dout[0]));
  assign alu_redesign_1_dout = cu_full1_1_c5 ? MBR_Content : 8'bz;  // Controlled_Buffer controlled_buffer_3
  MAR mar_1 (
    .Clock(clock_1_out), .WE(cu_full1_1_c9), .OE(cu_full1_1_c10), .Din(controlled_buffer_1_out),
    .Dout(mar_1_dout), .StoredData(MAR_Content));
  EightBitRegister MBR (
    .Clock(clock_1_out), .WE(cu_full1_1_c4), .OE(cu_full1_1_c6), .Din(alu_redesign_1_dout),
    .Dout(alu_redesign_1_dout), .StoredData(MBR_Content));
  EightBitRegister OutputRegister (
    .Clock(clock_1_out), .WE(cu_full1_1_c15), .OE(cu_full1_1_c14), .Din(alu_redesign_1_dout),
    .Dout(alu_redesign_1_dout), .StoredData(out_11));
  LED led_1 (.in(alu_redesign_1_dout[7]));
  LED led_2 (.in(alu_redesign_1_dout[6]));
  LED led_3 (.in(alu_redesign_1_dout[5]));
  LED led_4 (.in(alu_redesign_1_dout[4]));
  assign mar_1_dout = in_1 ? in_2 : 4'bz;  // Controlled_Buffer controlled_buffer_4
  LED led_5 (.in(alu_redesign_1_dout[3]));
  LED led_6 (.in(alu_redesign_1_dout[2]));
  LED led_7 (.in(alu_redesign_1_dout[1]));
  LED led_8 (.in(alu_redesign_1_dout[0]));
  RAM #(.addrWidth(4), .asyncread("true")) ram_1 (
    .addr(mar_1_dout), .we(cu_full1_1_c2), .oe(cu_full1_1_c3), .clk(clock_1_out), .din(alu_redesign_1_dout),
    .dout(ram_1_dout));
  Counter #(.max('h5), .width(3)) StepCounter (
    .count(1'b1), .Q(StepContent), .clk(clock_1_out));  // open: load, D, carry, up, clr
  assign alu_redesign_1_dout = cu_full1_1_c3 ? ram_1_dout : 8'bz;  // Controlled_Buffer controlled_buffer_5
  BitSelector #(.group(4)) bitselector_2 (.in(IR_content), .out(bitselector_2_out), .sel(1'b1));
  CU_FULL1 cu_full1_1 (
    .OPC3(bitselector_2_out[3]), .OPC2(bitselector_2_out[2]), .OPC1(bitselector_2_out[1]),
    .OPC0(bitselector_2_out[0]), .SC2(StepContent[2]), .SC1(StepContent[1]), .SC0(StepContent[0]),
    .C0(cu_full1_1_c0), .C1(cu_full1_1_c1), .C2(cu_full1_1_c2), .C3(cu_full1_1_c3), .C4(cu_full1_1_c4),
    .C5(cu_full1_1_c5), .C6(cu_full1_1_c6), .C7(cu_full1_1_c7), .C8(cu_full1_1_c8), .C9(cu_full1_1_c9),
    .C10(cu_full1_1_c10), .C11(cu_full1_1_c11), .C12(cu_full1_1_c12), .C13(cu_full1_1_c13),
    .C14(cu_full1_1_c14), .C15(cu_full1_1_c15), .C16(cu_full1_1_c16), .C17(cu_full1_1_c17),
    .C18(cu_full1_1_c18), .C19(cu_full1_1_c19));

  // Notes on the sheet:
  //   IR -> 
  //   PC .-> MAR -> RAM -> MBR - IR
  //   Internal Address Bus (4 bits)
  //   Internal Data Bus
  //   External Address Bus (4 bits)
  //   External Data Bus
  //   Load A - 0000
  //   Load B - 0001
  //   STORE - 0010
  //   ADD - 0011
  //   MULTIPLY - 0100
  //   OP Codes - Program Counter
  //   0 - 7 was instructions
  //   8 -15 data
  //   Subtraction Control
  //   ALU Direction
  //   C15
  //   C 14
  //   C 13
  //   C12
  //   C11
  //   C10
  //   C 9
  //   C 8
  //   C 7
  //   C 6
  //   C 5
  //   C 4
  //   C 3
  //   C 2
  //   C 1
  //   C 0
  //   C 19
  //   C 18
  //   C 17
  //   C 16
  //   OUPUT REG OE
  //   OUTPUT REG WE
  //   S0
  //   S1
  //   MAR WE
  //   MAR OE
  //   ALU OE
  //   REG A WE
  //   REG B WE
  //   PC Output Enable
  //   PC Count Enable
  //   RAM WE
  //   RAM OE
  //   MBR WE
  //   MBR Internal Bus Enable
  //   MBR OE
  //   IR WE
  //   IR OE
endmodule

module CU1 (
  input  OPC3,
  input  OPC2,
  input  OPC1,
  input  OPC0,
  input  SC2,
  input  SC1,
  input  SC0,
  output C0,
  output C1,
  output C2,
  output C3,
  output C4,
  output C5,
  output C6,
  output C7,
  output C8,
  output C9,
  output C10,
  output C11
);

  wire and_4_out, and_5_out, and_6_out, and_7_out, and_8_out, and_9_out, and_10_out, and_13_out, and_14_out,
       and_15_out, and_16_out, and_17_out, and_18_out, and_19_out, not_1_out, not_2_out, not_3_out,
       not_4_out, not_5_out;

  not not_1 (not_1_out, OPC1);
  not not_2 (not_2_out, OPC0);
  not not_3 (not_3_out, SC2);
  not not_4 (not_4_out, SC1);
  not not_5 (not_5_out, SC0);
  and and_1 (C0, not_3_out, not_4_out, not_5_out);
  and and_2 (C1, not_3_out, not_4_out, SC0);
  and and_3 (C2, OPC1, SC2);
  and and_4 (and_4_out, not_3_out, not_4_out, SC0);
  and and_5 (and_5_out, not_1_out, SC2, not_5_out);
  and and_6 (and_6_out, not_3_out, not_4_out, SC0);
  and and_7 (and_7_out, not_1_out, SC2, not_5_out);
  and and_8 (and_8_out, OPC1, OPC0, SC0);
  and and_9 (and_9_out, SC1, not_5_out);
  and and_10 (and_10_out, SC2, SC0);
  and and_11 (C6, OPC1, SC2);
  and and_12 (C7, SC1, not_5_out);
  and and_13 (and_13_out, not_1_out, SC1, SC0);
  and and_14 (and_14_out, OPC0, SC1, SC0);
  and and_15 (and_15_out, not_3_out, not_4_out, not_5_out);
  and and_16 (and_16_out, not_1_out, SC1, SC0);
  and and_17 (and_17_out, OPC0, SC1, SC0);
  and and_18 (and_18_out, not_3_out, not_4_out, SC0);
  and and_19 (and_19_out, SC2, not_5_out);
  and and_20 (C11, OPC1, not_2_out, SC1, SC0);
  or or_1 (C3, and_4_out, and_5_out);
  or or_2 (C4, and_6_out, and_7_out, and_8_out);
  or or_3 (C5, and_9_out, and_10_out);
  or or_4 (C8, and_13_out, and_14_out);
  or or_5 (C9, and_15_out, and_16_out, and_17_out);
  or or_6 (C10, and_18_out, and_19_out);
endmodule

module CU2 (
  input  OPC3,
  input  OPC2,
  input  OPC1,
  input  OPC0,
  input  SC2,
  input  SC1,
  input  SC0,
  output C12,
  output C13,
  output C14,
  output C15
);

  wire and_1_out, and_2_out, and_3_out, and_4_out, and_5_out, and_6_out, and_7_out, and_8_out, and_9_out,
       and_10_out, not_1_out, not_2_out, not_3_out, not_4_out;

  not not_1 (not_1_out, OPC1);
  not not_2 (not_2_out, OPC0);
  not not_3 (not_3_out, SC2);
  not not_4 (not_4_out, SC1);
  and and_1 (and_1_out, not_1_out, not_2_out, SC2, not_4_out, SC0);
  and and_2 (and_2_out, OPC2, not_2_out, SC2, SC0);
  and and_3 (and_3_out, OPC3, not_2_out, SC2, SC0);
  and and_4 (and_4_out, OPC1, not_2_out, SC2, SC1, SC0);
  and and_5 (and_5_out, not_1_out, OPC0, SC2, not_4_out, SC0);
  and and_6 (and_6_out, OPC2, OPC0, SC2, SC0);
  and and_7 (and_7_out, OPC3, OPC0, SC2, SC0);
  and and_8 (and_8_out, OPC1, OPC0, not_3_out, SC1, SC0);
  and and_9 (and_9_out, OPC2, OPC1, OPC0, SC1, SC0);
  and and_10 (and_10_out, OPC3, OPC1, OPC0, SC1, SC0);
  and and_11 (C15, OPC1, not_2_out, SC1, SC0);
  or or_1 (C12, and_1_out, and_2_out, and_3_out, and_4_out);
  or or_2 (C13, and_5_out, and_6_out, and_7_out);
  or or_3 (C14, and_8_out, and_9_out, and_10_out);
endmodule

module CU3 (
  input  OPC3,
  input  OPC2,
  input  OPC1,
  input  OPC0,
  input  SC2,
  input  SC1,
  input  SC0,
  output C16,
  output C17,
  output C18,
  output C19
);

  wire and_2_out, and_3_out, and_4_out, not_1_out, not_2_out, not_3_out, not_4_out;

  not not_1 (not_1_out, OPC2);
  not not_2 (not_2_out, OPC1);
  not not_3 (not_3_out, OPC0);
  not not_4 (not_4_out, SC2);
  and and_1 (C16, OPC2, not_2_out, not_4_out);
  and and_2 (and_2_out, OPC3, not_1_out, not_2_out, not_3_out, not_4_out);
  and and_3 (and_3_out, OPC2, not_2_out, OPC0, not_4_out);
  and and_4 (and_4_out, OPC2, OPC1, not_3_out, not_4_out);
  and and_5 (C18, OPC2, OPC1, OPC0);
  or or_1 (C17, and_2_out, and_3_out, and_4_out);

  assign C19 = OPC3;
endmodule

module CU_FULL (
  input  OPC3,
  input  OPC2,
  input  OPC1,
  input  OPC0,
  input  SC2,
  input  SC1,
  input  SC0,
  output C0,
  output C1,
  output C2,
  output C3,
  output C4,
  output C5,
  output C6,
  output C7,
  output C8,
  output C9,
  output C10,
  output C11,
  output C12,
  output C13,
  output C14,
  output C15,
  output C16,
  output C17,
  output C18,
  output C19
);

  wire and_4_out, and_5_out, and_6_out, and_7_out, and_8_out, and_9_out, and_10_out, and_13_out, and_14_out,
       and_15_out, and_16_out, and_17_out, and_18_out, and_19_out, and_20_out, and_21_out, and_22_out,
       and_23_out, and_24_out, and_25_out, and_26_out, and_27_out, and_28_out, and_29_out, and_30_out,
       and_31_out, and_32_out, and_33_out, and_34_out, and_35_out, and_36_out, and_40_out, and_41_out,
       and_42_out, and_43_out, and_44_out, and_45_out, and_46_out, and_47_out, and_48_out, and_49_out,
       and_50_out, and_52_out, not_1_out, not_2_out, not_3_out, not_4_out, not_5_out, not_6_out, not_7_out;

  not not_1 (not_1_out, OPC3);
  not not_2 (not_2_out, OPC2);
  not not_3 (not_3_out, OPC1);
  not not_4 (not_4_out, OPC0);
  not not_5 (not_5_out, SC2);
  not not_6 (not_6_out, SC1);
  not not_7 (not_7_out, SC0);
  and and_1 (C0, not_5_out, not_6_out, not_7_out);
  and and_2 (C1, not_5_out, not_6_out, SC0);
  and and_3 (C2, not_2_out, OPC1, not_4_out, SC2, not_7_out);
  and and_4 (and_4_out, not_5_out, not_6_out, SC0);
  and and_5 (and_5_out, not_2_out, not_3_out, SC2, not_7_out);
  and and_6 (and_6_out, not_5_out, not_6_out, SC0);
  and and_7 (and_7_out, not_2_out, not_3_out, SC2, not_7_out);
  and and_8 (and_8_out, not_2_out, OPC1, not_4_out, not_5_out, SC0);
  and and_9 (and_9_out, SC1, not_7_out);
  and and_10 (and_10_out, not_2_out, not_3_out, SC2, SC0);
  and and_11 (C6, not_2_out, OPC1, not_4_out, SC2, not_7_out);
  and and_12 (C7, SC1, not_7_out);
  and and_13 (and_13_out, not_2_out, OPC1, not_4_out, SC1, SC0);
  and and_14 (and_14_out, not_2_out, not_3_out, OPC0, SC1, SC0);
  and and_15 (and_15_out, not_1_out, not_2_out, not_4_out, SC1, SC0);
  and and_16 (and_16_out, not_2_out, not_4_out, SC2, SC1, SC0);
  and and_17 (and_17_out, not_5_out, not_6_out, not_7_out);
  and and_18 (and_18_out, not_2_out, not_3_out, OPC0, SC1, SC0);
  and and_19 (and_19_out, not_2_out, OPC1, not_4_out, SC1, SC0);
  and and_20 (and_20_out, not_1_out, not_2_out, not_4_out, SC1, SC0);
  and and_21 (and_21_out, not_2_out, not_4_out, SC2, SC1, SC0);
  and and_22 (and_22_out, not_5_out, not_6_out, SC0);
  and and_23 (and_23_out, OPC3, OPC2, not_6_out, not_7_out);
  and and_24 (and_24_out, OPC3, OPC0, not_6_out, not_7_out);
  and and_25 (and_25_out, OPC3, OPC1, not_6_out, not_7_out);
  and and_26 (and_26_out, not_1_out, not_2_out, not_3_out, SC2, not_7_out);
  and and_27 (and_27_out, not_2_out, not_3_out, SC2, SC1, not_7_out);
  and and_28 (and_28_out, not_1_out, not_2_out, not_4_out, SC2, not_7_out);
  and and_29 (and_29_out, not_2_out, not_4_out, SC2, SC1, not_7_out);
  and and_30 (and_30_out, OPC3, not_3_out, not_4_out, not_5_out, SC1, SC0);
  and and_31 (and_31_out, OPC3, SC2, SC1, not_7_out);
  and and_32 (and_32_out, OPC3, OPC0, SC1, not_7_out);
  and and_33 (and_33_out, OPC3, OPC1, SC1, not_7_out);
  and and_34 (and_34_out, not_1_out, OPC2, SC1, SC0);
  and and_35 (and_35_out, not_2_out, OPC1, OPC0, SC1, SC0);
  and and_36 (and_36_out, OPC3, OPC2, not_3_out, SC1);
  and and_37 (C12, not_2_out, not_3_out, not_4_out, SC2, SC0);
  and and_38 (C13, not_2_out, not_3_out, OPC0, SC2, SC0);
  and and_39 (C14, not_2_out, OPC1, not_4_out, SC1, SC0);
  and and_40 (and_40_out, OPC3, not_3_out, not_4_out, not_5_out, SC1, SC0);
  and and_41 (and_41_out, OPC2, not_3_out, SC1, SC0);
  and and_42 (and_42_out, OPC2, not_4_out, SC1, SC0);
  and and_43 (and_43_out, not_2_out, OPC1, OPC0, SC1, SC0);
  and and_44 (and_44_out, not_1_out, OPC1, OPC0, SC1, SC0);
  and and_45 (and_45_out, OPC3, OPC2, not_3_out, not_5_out);
  and and_46 (and_46_out, OPC2, not_3_out, OPC0, not_5_out);
  and and_47 (and_47_out, OPC3, not_2_out, not_3_out, not_4_out, not_5_out);
  and and_48 (and_48_out, OPC2, not_3_out, OPC0, not_5_out);
  and and_49 (and_49_out, OPC2, OPC1, not_4_out, not_5_out);
  and and_50 (and_50_out, not_1_out, OPC2, not_4_out, not_5_out);
  and and_51 (C18, OPC2, OPC1, OPC0);
  and and_52 (and_52_out, OPC2, not_3_out, not_4_out, not_5_out);
  or or_1 (C3, and_4_out, and_5_out);
  or or_2 (C4, and_6_out, and_7_out, and_8_out);
  or or_3 (C5, and_9_out, and_10_out);
  or or_4 (C8, and_13_out, and_14_out, and_15_out, and_16_out);
  or or_5 (C9, and_17_out, and_18_out, and_19_out, and_20_out, and_21_out);
  or or_6 (C10, and_22_out, and_23_out, and_24_out, and_25_out, and_26_out, and_27_out, and_28_out, and_29_out);
  or or_7 (C11, and_30_out, and_31_out, and_32_out, and_33_out, and_34_out, and_35_out, and_36_out);
  or or_8 (C15, and_40_out, and_41_out, and_42_out, and_43_out, and_44_out);
  or or_9 (C16, and_45_out, and_46_out);
  or or_10 (C17, and_47_out, and_48_out, and_49_out, and_50_out);
  or or_11 (C19, and_52_out, OPC3);
endmodule

module CU_FULL1 (
  input  OPC3,
  input  OPC2,
  input  OPC1,
  input  OPC0,
  input  SC2,
  input  SC1,
  input  SC0,
  output C0,
  output C1,
  output C2,
  output C3,
  output C4,
  output C5,
  output C6,
  output C7,
  output C8,
  output C9,
  output C10,
  output C11,
  output C12,
  output C13,
  output C14,
  output C15,
  output C16,
  output C17,
  output C18,
  output C19
);

  wire and_4_out, and_5_out, and_6_out, and_7_out, and_8_out, and_9_out, and_10_out, and_13_out, and_14_out,
       and_15_out, and_16_out, and_17_out, and_18_out, and_19_out, and_20_out, and_21_out, and_22_out,
       and_23_out, and_24_out, and_25_out, and_26_out, and_27_out, and_28_out, and_29_out, and_30_out,
       and_31_out, and_32_out, and_33_out, and_34_out, and_35_out, and_36_out, and_40_out, and_41_out,
       and_42_out, and_43_out, and_44_out, and_45_out, and_46_out, and_47_out, and_48_out, and_49_out,
       and_50_out, and_52_out, not_1_out, not_2_out, not_3_out, not_4_out, not_5_out, not_6_out, not_7_out;

  not not_1 (not_1_out, OPC3);
  not not_2 (not_2_out, OPC2);
  not not_3 (not_3_out, OPC1);
  not not_4 (not_4_out, OPC0);
  not not_5 (not_5_out, SC2);
  not not_6 (not_6_out, SC1);
  not not_7 (not_7_out, SC0);
  and and_1 (C0, not_5_out, not_6_out, not_7_out);
  and and_2 (C1, not_5_out, not_6_out, SC0);
  and and_3 (C2, not_2_out, OPC1, not_4_out, SC2, not_7_out);
  and and_4 (and_4_out, not_5_out, not_6_out, SC0);
  and and_5 (and_5_out, not_2_out, not_3_out, SC2, not_7_out);
  and and_6 (and_6_out, not_5_out, not_6_out, SC0);
  and and_7 (and_7_out, not_2_out, not_3_out, SC2, not_7_out);
  and and_8 (and_8_out, not_2_out, OPC1, not_4_out, not_5_out, SC0);
  and and_9 (and_9_out, SC1, not_7_out);
  and and_10 (and_10_out, not_2_out, not_3_out, SC2, SC0);
  and and_11 (C6, not_2_out, OPC1, not_4_out, SC2, not_7_out);
  and and_12 (C7, SC1, not_7_out);
  and and_13 (and_13_out, not_2_out, OPC1, not_4_out, SC1, SC0);
  and and_14 (and_14_out, not_2_out, not_3_out, OPC0, SC1, SC0);
  and and_15 (and_15_out, not_1_out, not_2_out, not_4_out, SC1, SC0);
  and and_16 (and_16_out, not_2_out, not_4_out, SC2, SC1, SC0);
  and and_17 (and_17_out, not_5_out, not_6_out, not_7_out);
  and and_18 (and_18_out, not_2_out, not_3_out, OPC0, SC1, SC0);
  and and_19 (and_19_out, not_2_out, OPC1, not_4_out, SC1, SC0);
  and and_20 (and_20_out, not_1_out, not_2_out, not_4_out, SC1, SC0);
  and and_21 (and_21_out, not_2_out, not_4_out, SC2, SC1, SC0);
  and and_22 (and_22_out, not_5_out, not_6_out, SC0);
  and and_23 (and_23_out, OPC3, OPC2, not_6_out, not_7_out);
  and and_24 (and_24_out, OPC3, OPC0, not_6_out, not_7_out);
  and and_25 (and_25_out, OPC3, OPC1, not_6_out, not_7_out);
  and and_26 (and_26_out, not_1_out, not_2_out, not_3_out, SC2, not_7_out);
  and and_27 (and_27_out, not_2_out, not_3_out, SC2, SC1, not_7_out);
  and and_28 (and_28_out, not_1_out, not_2_out, not_4_out, SC2, not_7_out);
  and and_29 (and_29_out, not_2_out, not_4_out, SC2, SC1, not_7_out);
  and and_30 (and_30_out, OPC3, not_3_out, not_4_out, not_5_out, SC1, SC0);
  and and_31 (and_31_out, OPC3, SC2, SC1, not_7_out);
  and and_32 (and_32_out, OPC3, OPC0, SC1, not_7_out);
  and and_33 (and_33_out, OPC3, OPC1, SC1, not_7_out);
  and and_34 (and_34_out, not_1_out, OPC2, SC1, SC0);
  and and_35 (and_35_out, not_2_out, OPC1, OPC0, SC1, SC0);
  and and_36 (and_36_out, OPC3, OPC2, not_3_out, SC1);
  and and_37 (C12, not_2_out, not_3_out, not_4_out, SC2, SC0);
  and and_38 (C13, not_2_out, not_3_out, OPC0, SC2, SC0);
  and and_39 (C14, not_2_out, OPC1, not_4_out, SC1, SC0);
  and and_40 (and_40_out, OPC3, not_3_out, not_4_out, not_5_out, SC1, SC0);
  and and_41 (and_41_out, OPC2, not_3_out, SC1, SC0);
  and and_42 (and_42_out, OPC2, not_4_out, SC1, SC0);
  and and_43 (and_43_out, not_2_out, OPC1, OPC0, SC1, SC0);
  and and_44 (and_44_out, not_1_out, OPC1, OPC0, SC1, SC0);
  and and_45 (and_45_out, OPC3, OPC2, not_3_out, not_5_out);
  and and_46 (and_46_out, OPC2, not_3_out, OPC0, not_5_out);
  and and_47 (and_47_out, OPC3, not_2_out, not_3_out, not_4_out, not_5_out);
  and and_48 (and_48_out, OPC2, not_3_out, OPC0, not_5_out);
  and and_49 (and_49_out, OPC2, OPC1, not_4_out, not_5_out);
  and and_50 (and_50_out, not_1_out, OPC2, not_4_out, not_5_out);
  and and_51 (C18, OPC2, OPC1, OPC0);
  and and_52 (and_52_out, OPC2, not_3_out, not_4_out, not_5_out);
  or or_1 (C3, and_4_out, and_5_out);
  or or_2 (C4, and_6_out, and_7_out, and_8_out);
  or or_3 (C5, and_9_out, and_10_out);
  or or_4 (C8, and_13_out, and_14_out, and_15_out, and_16_out);
  or or_5 (C9, and_17_out, and_18_out, and_19_out, and_20_out, and_21_out);
  or or_6 (C10, and_22_out, and_23_out, and_24_out, and_25_out, and_26_out, and_27_out, and_28_out, and_29_out);
  or or_7 (C11, and_30_out, and_31_out, and_32_out, and_33_out, and_34_out, and_35_out, and_36_out);
  or or_8 (C15, and_40_out, and_41_out, and_42_out, and_43_out, and_44_out);
  or or_9 (C16, and_45_out, and_46_out);
  or or_10 (C17, and_47_out, and_48_out, and_49_out, and_50_out);
  or or_11 (C19, and_52_out, OPC3);
endmodule
